// Logisim project mycpu.circ as structural Verilog: 9 circuits, main circuit main
module main (
  input  in_1,
  output [31:0] out_2,
  output [31:0] out_3,
  output out_4,
  output [4:0] out_5,
  output [31:0] out_6,
  output out_7,
  output [31:0] out_8,
  output [31:0] out_9
);

  wire clk, ctrl_1_alusrc, ctrl_1_beq, ctrl_1_jr, ctrl_1_memtoreg, ctrl_1_regdst, EXTOp, JAL, zero;
  wire [1:0] ctrl_1_aluop, ctrl_1_regwrop, npcop_1_npcop;
  wire [31:0] dm_1_rd, GRF_rs, imm32, multiplexer_1_out, PC_4, RegData;

  NPCOp npcop_1 (.BEQ(ctrl_1_beq), .zero(zero), .JAL(JAL), .NPCOp(npcop_1_npcop), .jr(ctrl_1_jr));
  IFU ifu_1 (
    .clk(clk), .rst(in_1), .inStr(out_2), .NPCOp(npcop_1_npcop), .out_9(out_3), .imm(imm32),
    .instr_index(out_2[25:0]), .PC_4(PC_4), .GRF_rs(GRF_rs));
  CTRL ctrl_1 (
    .op(out_2[31:26]), .func(out_2[5:0]), .RegDst(ctrl_1_regdst), .ALUOp(ctrl_1_aluop),
    .ALUSrc(ctrl_1_alusrc), .RegWr(out_4), .MemWr(out_7), .beq(ctrl_1_beq), .MemToReg(ctrl_1_memtoreg),
    .EXTOp(EXTOp), .RegWrOp(ctrl_1_regwrop), .JAL(JAL), .jr(ctrl_1_jr));
  RegWrite regwrite_1 (
    .rt(out_2[20:16]), .imm16(out_2[15:0]), .rd(out_2[15:11]), .PC_4(PC_4), .RegData(RegData),
    .RegWrAddr(out_5), .RegDst(ctrl_1_regdst), .jal(JAL), .RegWrOp(ctrl_1_regwrop), .out_10(out_6));
  EXT ext_1 (.in_2(out_2[15:0]), .out_3(imm32), .EXTOp(EXTOp));
  GRF grf_1 (
    .A1(out_2[25:21]), .A2(out_2[20:16]), .A3(out_5), .WD(out_6), .out_8(GRF_rs), .out_9(out_9), .clk(clk),
    .reset(in_1), .WE(out_4));
  Multiplexer #(.width(32)) multiplexer_1 (
    .in0(out_9), .in1(imm32), .out(multiplexer_1_out), .sel(ctrl_1_alusrc));  // open: en
  ALU alu_1 (.SrcA(GRF_rs), .SrcB(multiplexer_1_out), .out_5(out_8), .ALUOp(ctrl_1_aluop), .zero(zero));
  Multiplexer #(.width(32)) multiplexer_2 (
    .in0(out_8), .in1(dm_1_rd), .out(RegData), .sel(ctrl_1_memtoreg));  // open: en
  DM dm_1 (.Address(out_8), .WD(out_9), .clk(clk), .reset(in_1), .MemWrite(out_7), .RD(dm_1_rd));
  Clock clock_1 (.out(clk));

  // Other names for the same wires on the sheet: imm16[15:0] = out_2[15:0]; Instr[31:0] = out_2;
  //   instr_index[25:0] = out_2[25:0]; MemAddr[31:0] = out_8; MemData[31:0] = out_9; MemWr = out_7; PC[31:0] = out_3;
  //   RegAddr[4:0] = out_5; RegWr = out_4; RegWrData[31:0] = out_6; rst = in_1

  // Notes on the sheet:
  //   op
  //   funct
  //   rt
  //   rd
  //   RegWrOp
  //   RegDst
  //   GRF Write
  //   rs
  //   R1
  //   rt
  //   R2
  //   W
  //   WD
  //   RD1
  //   RD2
  //   ALUSrc
  //   ALUOp
  //   WE
  //   A
  //   RD
  //   WD
  //   rst
  //   MemToReg
endmodule

module CTRL (
  input  [5:0] op,
  input  [5:0] func,
  output RegDst,
  output [1:0] ALUOp,
  output ALUSrc,
  output RegWr,
  output [1:0] RegWrOp,
  output MemWr,
  output beq,
  output MemToReg,
  output EXTOp,
  output JAL,
  output jr
);

  wire ADD, add_out, BEQ_t, LUI, LW, not_1_out, not_2_out, not_3_out, not_4_out, not_5_out, not_6_out,
       not_7_out, not_8_out, not_9_out, not_10_out, not_11_out, not_12_out, or_out, ORI, R, sll_out, SUB,
       sub_out, SW, undriven;

  not not_1 (not_1_out, op[4]);
  not not_2 (not_2_out, op[5]);
  not not_3 (not_3_out, op[3]);
  not not_4 (not_4_out, op[2]);
  not not_5 (not_5_out, op[0]);
  not not_6 (not_6_out, op[1]);
  not not_7 (not_7_out, func[4]);
  not not_8 (not_8_out, func[5]);
  not not_9 (not_9_out, func[3]);
  not not_10 (not_10_out, func[2]);
  not not_11 (not_11_out, func[1]);
  not not_12 (not_12_out, func[0]);
  and and_1 (R, not_5_out, not_6_out, not_4_out, not_3_out, not_1_out, not_2_out);
  and and_2 (ADD, R, not_12_out, not_11_out, not_10_out, not_9_out, not_7_out, func[5]);
  and and_3 (SUB, R, not_12_out, func[1], not_10_out, not_9_out, not_7_out, func[5]);
  and and_4 (ORI, op[0], not_6_out, op[2], op[3], not_1_out, not_2_out);
  and and_5 (LW, op[0], op[1], not_4_out, not_3_out, not_1_out, op[5]);
  and and_6 (SW, op[0], op[1], not_4_out, op[3], not_1_out, op[5]);
  and and_7 (BEQ_t, not_5_out, not_6_out, op[2], not_3_out, not_1_out, not_2_out);
  and and_8 (LUI, op[0], op[1], op[2], op[3], not_1_out, not_2_out);
  and and_9 (JAL, op[0], op[1], not_4_out, not_3_out, not_1_out, not_2_out);
  and and_10 (jr, R, not_12_out, not_11_out, not_10_out, func[3], not_7_out, not_8_out);
  or u_add (add_out, ADD, LW, SW);
  or u_sub (sub_out, SUB, BEQ_t);
  buf \or  (or_out, ORI);  // OR_Gate
  buf sll (sll_out, undriven);  // OR_Gate
  or _1 (ALUSrc, ORI, LW, SW);
  or or_2 (RegWrOp[0], 1'b0, LUI);
  or or_3 (RegDst, ADD, SUB);
  or _1_2 (RegWr, ADD, SUB, ORI, LW, LUI, JAL);
  buf _1_3 (MemWr, SW);  // OR_Gate
  buf _1_4 (beq, BEQ_t);  // OR_Gate
  buf _1_5 (MemToReg, LW);  // OR_Gate
  or _1_6 (EXTOp, LW, SW, BEQ_t);
  buf _0 (ALUOp[0], sub_out);  // OR_Gate
  buf _1_7 (ALUOp[1], or_out);  // OR_Gate

  assign RegWrOp[1] = JAL;
endmodule

module IFU (
  input  clk,
  input  [31:0] imm,
  input  rst,
  input  [1:0] NPCOp,
  input  [25:0] instr_index,
  input  [31:0] GRF_rs,
  output [31:0] PC_4,
  output [31:0] inStr,
  output [31:0] out_9
);

  wire comparator_1_eq;
  wire [11:0] subtractor_1_out;
  wire [15:0] shifter_1_out;
  wire [31:0] adder_2_out, bit_extender_1_out, NPC, register_1_q;

  Shifter #(.width(16)) shifter_1 (.in(imm[15:0]), .\dist (4'b0010), .out(shifter_1_out));
  Register #(.width(32)) register_1 (.D(NPC), .Q(register_1_q), .clk(clk), .clr(rst));  // open: en
  assign bit_extender_1_out = {{16{shifter_1_out[15]}}, shifter_1_out};  // Bit_Extender bit_extender_1
  Adder #(.width(32)) adder_1 (.a(32'h4), .b(out_9), .out(PC_4));  // open: cin, cout
  Adder #(.width(32)) adder_2 (.a(PC_4), .b(bit_extender_1_out), .out(adder_2_out));  // open: cin, cout
  Comparator #(.width(32)) comparator_1 (.a(register_1_q), .b({32{1'b0}}), .eq(comparator_1_eq));  // open: gt, lt
  Multiplexer #(.width(32)) multiplexer_1 (
    .in0(register_1_q), .in1(32'h3000), .out(out_9), .sel(comparator_1_eq));  // open: en
  // Probe on subtractor_1_out
  // Probe on NPC
  Multiplexer #(.select(2), .width(32)) multiplexer_2 (
    .in0(PC_4), .in1(adder_2_out), .in2({out_9[31:28], instr_index, 2'b00}), .in3(GRF_rs), .out(NPC),
    .sel(NPCOp));  // open: en
  Subtractor #(.width(12)) subtractor_1 (.a(out_9[13:2]), .b(12'hc00), .out(subtractor_1_out));  // open: bin, bout
  // Probe on out_9
  ROM #(.addrWidth(12), .dataWidth(32)) rom_1 (.addr(subtractor_1_out), .data(inStr));  // open: sel

  // Other names for the same wires on the sheet: instr_index_25[25:0] = instr_index; PC[31:0] = out_9;
  //   imm32[31:0] = imm; reset = rst

  // Notes on the sheet:
  //   PC + 4
  //   BEQ
  //   JAL
  //   jr
  //   contents of rom_1 (hex, n*v repeats v):
  //   3c032766 c000c03 34630000 631820 3e00008
endmodule

module GRF (
  input  clk,
  input  reset,
  input  WE,
  input  [4:0] A1,
  input  [4:0] A2,
  input  [4:0] A3,
  input  [31:0] WD,
  output [31:0] out_8,
  output [31:0] out_9
);

  wire [31:0] out00, out01, out02, out03, out04, out05, out06, out07, out08, out09, out10, out11, out12,
       out13, out14, out15, out16, out17, out18, out19, out20, out21, out22, out23, out24, out25, out26,
       out27, out28, out29, out30, out31, wr01, wr02, wr03, wr04, wr05, wr06, wr07, wr08, wr09, wr10, wr11,
       wr12, wr13, wr14, wr15, wr16, wr17, wr18, wr19, wr20, wr21, wr22, wr23, wr24, wr25, wr26, wr27, wr28,
       wr29, wr30, wr31;

  Multiplexer #(.select(5), .width(32)) multiplexer_1 (
    .in0(out00), .in1(out01), .in2(out02), .in3(out03), .in4(out04), .in5(out05), .in6(out06), .in7(out07),
    .in8(out08), .in9(out09), .in10(out10), .in11(out11), .in12(out12), .in13(out13), .in14(out14),
    .in15(out15), .in16(out16), .in17(out17), .in18(out18), .in19(out19), .in20(out20), .in21(out21),
    .in22(out22), .in23(out23), .in24(out24), .in25(out25), .in26(out26), .in27(out27), .in28(out28),
    .in29(out29), .in30(out30), .in31(out31), .out(out_9), .sel(A2));  // open: en
  Register #(.width(32)) register_1 (.D({32{1'b0}}), .en(WE), .Q(out00), .clk(clk), .clr(reset));
  Register #(.width(32)) register_2 (.D(wr08), .en(WE), .Q(out08), .clk(clk), .clr(reset));
  Register #(.width(32)) register_3 (.D(wr16), .en(WE), .Q(out16), .clk(clk), .clr(reset));
  Register #(.width(32)) register_4 (.D(wr24), .en(WE), .Q(out24), .clk(clk), .clr(reset));
  Register #(.width(32)) register_5 (.D(wr01), .en(WE), .Q(out01), .clk(clk), .clr(reset));
  Register #(.width(32)) register_6 (.D(wr09), .en(WE), .Q(out09), .clk(clk), .clr(reset));
  Register #(.width(32)) register_7 (.D(wr17), .en(WE), .Q(out17), .clk(clk), .clr(reset));
  Register #(.width(32)) register_8 (.D(wr25), .en(WE), .Q(out25), .clk(clk), .clr(reset));
  Register #(.width(32)) register_9 (.D(wr02), .en(WE), .Q(out02), .clk(clk), .clr(reset));
  Register #(.width(32)) register_10 (.D(wr10), .en(WE), .Q(out10), .clk(clk), .clr(reset));
  Register #(.width(32)) register_11 (.D(wr18), .en(WE), .Q(out18), .clk(clk), .clr(reset));
  Register #(.width(32)) register_12 (.D(wr26), .en(WE), .Q(out26), .clk(clk), .clr(reset));
  Register #(.width(32)) register_13 (.D(wr03), .en(WE), .Q(out03), .clk(clk), .clr(reset));
  Register #(.width(32)) register_14 (.D(wr11), .en(WE), .Q(out11), .clk(clk), .clr(reset));
  Register #(.width(32)) register_15 (.D(wr19), .en(WE), .Q(out19), .clk(clk), .clr(reset));
  Register #(.width(32)) register_16 (.D(wr27), .en(WE), .Q(out27), .clk(clk), .clr(reset));
  Multiplexer #(.select(5), .width(32)) multiplexer_2 (
    .in0(out00), .in1(out01), .in2(out02), .in3(out03), .in4(out04), .in5(out05), .in6(out06), .in7(out07),
    .in8(out08), .in9(out09), .in10(out10), .in11(out11), .in12(out12), .in13(out13), .in14(out14),
    .in15(out15), .in16(out16), .in17(out17), .in18(out18), .in19(out19), .in20(out20), .in21(out21),
    .in22(out22), .in23(out23), .in24(out24), .in25(out25), .in26(out26), .in27(out27), .in28(out28),
    .in29(out29), .in30(out30), .in31(out31), .out(out_8), .sel(A1));  // open: en
  Register #(.width(32)) register_17 (.D(wr04), .en(WE), .Q(out04), .clk(clk), .clr(reset));
  Register #(.width(32)) register_18 (.D(wr12), .en(WE), .Q(out12), .clk(clk), .clr(reset));
  Register #(.width(32)) register_19 (.D(wr20), .en(WE), .Q(out20), .clk(clk), .clr(reset));
  Register #(.width(32)) register_20 (.D(wr28), .en(WE), .Q(out28), .clk(clk), .clr(reset));
  // Probe on wr01
  Demultiplexer #(.select(5), .width(32), .tristate("true")) demultiplexer_1 (
    .out1(wr01), .out2(wr02), .out3(wr03), .out4(wr04), .out5(wr05), .out6(wr06), .out7(wr07), .out8(wr08),
    .out9(wr09), .out10(wr10), .out11(wr11), .out12(wr12), .out13(wr13), .out14(wr14), .out15(wr15),
    .out16(wr16), .out17(wr17), .out18(wr18), .out19(wr19), .out20(wr20), .out21(wr21), .out22(wr22),
    .out23(wr23), .out24(wr24), .out25(wr25), .out26(wr26), .out27(wr27), .out28(wr28), .out29(wr29),
    .out30(wr30), .out31(wr31), .in(WD), .sel(A3));  // open: out0, en
  Register #(.width(32)) register_21 (.D(wr05), .en(WE), .Q(out05), .clk(clk), .clr(reset));
  Register #(.width(32)) register_22 (.D(wr13), .en(WE), .Q(out13), .clk(clk), .clr(reset));
  Register #(.width(32)) register_23 (.D(wr21), .en(WE), .Q(out21), .clk(clk), .clr(reset));
  Register #(.width(32)) register_24 (.D(wr29), .en(WE), .Q(out29), .clk(clk), .clr(reset));
  Register #(.width(32)) register_25 (.D(wr06), .en(WE), .Q(out06), .clk(clk), .clr(reset));
  Register #(.width(32)) register_26 (.D(wr14), .en(WE), .Q(out14), .clk(clk), .clr(reset));
  Register #(.width(32)) register_27 (.D(wr22), .en(WE), .Q(out22), .clk(clk), .clr(reset));
  Register #(.width(32)) register_28 (.D(wr30), .en(WE), .Q(out30), .clk(clk), .clr(reset));
  Register #(.width(32)) register_29 (.D(wr07), .en(WE), .Q(out07), .clk(clk), .clr(reset));
  Register #(.width(32)) register_30 (.D(wr15), .en(WE), .Q(out15), .clk(clk), .clr(reset));
  Register #(.width(32)) register_31 (.D(wr23), .en(WE), .Q(out23), .clk(clk), .clr(reset));
  Register #(.width(32)) register_32 (.D(wr31), .en(WE), .Q(out31), .clk(clk), .clr(reset));

  // Other names for the same wires on the sheet: RD1[31:0] = out_8; RD2[31:0] = out_9
endmodule

module ALU (
  input  [1:0] ALUOp,
  input  [31:0] SrcA,
  input  [31:0] SrcB,
  output zero,
  output [31:0] out_5
);

  wire [31:0] adder_1_out, or_1_out, shifter_1_out, subtractor_1_out;

  Adder #(.width(32)) adder_1 (.a(SrcA), .b(SrcB), .out(adder_1_out));  // open: cin, cout
  Subtractor #(.width(32)) subtractor_1 (.a(SrcA), .b(SrcB), .out(subtractor_1_out));  // open: bin, bout
  assign or_1_out = SrcA | SrcB;  // OR_Gate or_1, 32 bits wide
  Shifter #(.width(32)) shifter_1 (.in(SrcA), .\dist (SrcB[4:0]), .out(shifter_1_out));
  Multiplexer #(.select(2), .width(32)) multiplexer_1 (
    .in0(adder_1_out), .in1(subtractor_1_out), .in2(or_1_out), .in3(shifter_1_out), .out(out_5), .sel(ALUOp));  // open: en
  Comparator #(.width(32)) comparator_1 (.a(out_5), .b({32{1'b0}}), .eq(zero));  // open: gt, lt
endmodule

module EXT (
  input  EXTOp,
  input  [15:0] in_2,
  output [31:0] out_3
);

  wire [31:0] bit_extender_1_out, bit_extender_2_out;

  assign bit_extender_1_out = {{16{1'b0}}, in_2};  // Bit_Extender bit_extender_1
  assign bit_extender_2_out = {{16{in_2[15]}}, in_2};  // Bit_Extender bit_extender_2
  Multiplexer #(.width(32)) multiplexer_1 (
    .in0(bit_extender_1_out), .in1(bit_extender_2_out), .out(out_3), .sel(EXTOp));  // open: en
endmodule

module DM (
  input  [31:0] Address,
  input  [31:0] WD,
  input  clk,
  input  reset,
  input  MemWrite,
  output [31:0] RD
);

  // Probe on Address[13:0]
  RAM #(.addrWidth(14), .dataWidth(32), .bus("separate")) ram_1 (
    .addr(Address[13:0]), .din(WD), .data(RD), .str(MemWrite), .clk(clk), .clr(reset));  // open: sel, ld

  // Other names for the same wires on the sheet: WE = MemWrite

  // Notes on the sheet:
  //   WD: 32bits
  //   Adress: 14bits 
endmodule

module NPCOp (
  input  BEQ,
  input  zero,
  input  JAL,
  input  jr,
  output [1:0] NPCOp
);

  wire and_1_out;

  and and_1 (and_1_out, BEQ, zero);
  or or_1 (NPCOp[1], JAL, jr);
  or or_2 (NPCOp[0], jr, and_1_out);
endmodule

module RegWrite (
  input  [4:0] rt,
  input  [4:0] rd,
  input  RegDst,
  input  jal,
  input  [15:0] imm16,
  input  [31:0] PC_4,
  input  [31:0] RegData,
  input  [1:0] RegWrOp,
  output [4:0] RegWrAddr,
  output [31:0] out_10
);

  wire [4:0] multiplexer_1_out;

  Multiplexer #(.width(5)) multiplexer_1 (.in0(rt), .in1(rd), .out(multiplexer_1_out), .sel(RegDst));  // open: en
  Multiplexer #(.width(5)) multiplexer_2 (
    .in0(multiplexer_1_out), .in1({5{1'b1}}), .out(RegWrAddr), .sel(jal));  // open: en
  Multiplexer #(.select(2), .width(32)) multiplexer_3 (
    .in0(RegData), .in1({imm16, {16{1'b0}}}), .in2(PC_4), .out(out_10), .sel(RegWrOp));  // open: in3, en

  // Notes on the sheet:
  //   Address
  //   Write to $ra
  //   Data
endmodule
